// Logisim project 2.circ as structural Verilog: 1 circuit, main circuit main
module main (
  input  A,
  input  B,
  input  C,
  output A_prime_B_prime_C_AB
);

  wire and_1_out, and_2_out, not_1_out, not_2_out;

  not not_1 (not_1_out, A);
  not not_2 (not_2_out, B);
  and and_1 (and_1_out, not_1_out, not_2_out);
  and and_2 (and_2_out, A, B);
  or or_1 (A_prime_B_prime_C_AB, and_1_out, C, and_2_out);

  // Notes on the sheet:
  //   A'B'
  //   C
  //   AB
endmodule
