// Logisim project FUll adder.circ as structural Verilog: 1 circuit, main circuit main
module main (
  input  A,
  input  B,
  input  C,
  output out_4,
  output C_A_XOR_B____A_B
);

  wire and_1_out, and_2_out, xor_1_out;

  xor xor_1 (xor_1_out, A, B);
  and and_1 (and_1_out, xor_1_out, C);
  and and_2 (and_2_out, A, B);
  xor xor_2 (out_4, xor_1_out, C);
  or or_1 (C_A_XOR_B____A_B, and_1_out, and_2_out);

  // Notes on the sheet:
  //   MD.MAhfujur Rahman ID : 192311014
  //   A XOR B
  //   A XOR B XOR C
  //   (A XOR B).C
  //   A.B
endmodule
