// Logisim project a1.circ as structural Verilog: 1 circuit, main circuit main
module main (
  input  a,
  input  b,
  input  c,
  input  d,
  output b_prime_d_bd_prime_cd_prime
);

  wire and_1_out, and_2_out, and_3_out, not_1_out, not_2_out, not_3_out;

  not not_1 (not_1_out, b);
  not not_2 (not_2_out, d);
  not not_3 (not_3_out, d);
  and and_1 (and_1_out, not_1_out, d);
  and and_2 (and_2_out, b, not_2_out);
  and and_3 (and_3_out, c, not_3_out);
  or or_1 (b_prime_d_bd_prime_cd_prime, and_1_out, and_2_out, and_3_out);

  // Notes on the sheet:
  //   MD.Mahfujur Rahman 
  //   ID: 192311014
endmodule
