// Logisim project addar.circ as structural Verilog: 1 circuit, main circuit main
module main (
  input  A,
  input  B,
  output out_3,
  output out_4
);

  xor xor_1 (out_3, A, B);
  and and_1 (out_4, A, B);

  // Notes on the sheet:
  //   MD.Mahfujur Rahman ID:192311014
  //   Sum A xor B
  //   Carry A.B
endmodule
