// Logisim project decoder.circ as structural Verilog: 1 circuit, main circuit main
module main (
  input  A0,
  input  A1,
  input  E,
  output Y3,
  output Y2,
  output Y1,
  output Y0
);

  wire not_1_out, not_2_out, not_3_out, not_4_out;

  not not_1 (not_1_out, A0);
  not not_2 (not_2_out, A1);
  not not_3 (not_3_out, A0);
  not not_4 (not_4_out, A1);
  and and_1 (Y3, A0, A1, E);
  and and_2 (Y2, not_1_out, A1, E);
  and and_3 (Y1, A0, not_2_out, E);
  and and_4 (Y0, not_3_out, not_4_out, E);

  // Notes on the sheet:
  //   MD.Mahfujur Rahman ID:192311014
endmodule
