// Logisim project encoder.circ as structural Verilog: 1 circuit, main circuit main
module main (
  input  Y1,
  input  Y2,
  input  Y3,
  input  A1_Y1_Y3,
  input  A0_Y2_Y3
);

  wire or_1_out, or_2_out;

  or or_1 (or_1_out, Y1, Y3);
  or or_2 (or_2_out, Y2, Y3);

  // Notes on the sheet:
  //   MD.Mahfujur Rahman ID:192311014
endmodule
