// Logisim project full adder.circ as structural Verilog: 1 circuit, main circuit main
module main (
  input  A,
  input  B,
  input  Cin,
  output out_4,
  output out_5
);

  wire and_1_out, and_2_out, xor_1_out;

  xor xor_1 (xor_1_out, A, B);
  and and_1 (and_1_out, A, B);
  and and_2 (and_2_out, xor_1_out, Cin);
  or or_1 (out_5, and_1_out, and_2_out);
  xor xor_2 (out_4, xor_1_out, Cin);

  // Notes on the sheet:
  //   MD.Mahfujur Rahman ID:192311014
  //   Carry A.B
  //   Sum A xor B
  //   Sum (A xor B) xor Cin
  //   Carry A.B+Cin(A xor B)
endmodule
