// Logisim project sub.circ as structural Verilog: 1 circuit, main circuit main
module main (
  input  A,
  input  B,
  output out_3,
  output out_4
);

  wire not_1_out;

  not not_1 (not_1_out, A);
  xor xor_1 (out_3, A, B);
  and and_1 (out_4, not_1_out, B);

  // Notes on the sheet:
  //   Sum
  //   Carry
endmodule
